// Logisim project 7bitXOR.circ as structural Verilog: 1 circuit, main circuit main
module main (
  input  in_1,
  input  in_2,
  input  in_3,
  input  in_4,
  input  in_5,
  input  in_6,
  input  in_7,
  input  in_8,
  input  in_9,
  input  in_10,
  input  in_11,
  input  in_12,
  input  in_13,
  input  in_14,
  input  in_15,
  input  in_16,
  output out_17,
  output out_18
);

  wire odd_parity_1_out, xor_1_out, xor_2_out, xor_3_out, xor_4_out, xor_5_out, xor_6_out;

  xor xor_1 (xor_1_out, in_2, in_3);
  xor xor_2 (xor_2_out, in_4, in_5);
  xor xor_3 (xor_3_out, in_6, in_7);
  xor xor_4 (xor_4_out, xor_1_out, xor_2_out);
  xor xor_5 (xor_5_out, xor_3_out, in_8);
  xor odd_parity_1 (odd_parity_1_out, in_9, in_10, in_11, in_12, in_13, in_14, in_15);
  xor xor_6 (xor_6_out, xor_4_out, xor_5_out);
  xor odd_parity_2 (out_18, odd_parity_1_out, in_16);
  xor xor_7 (out_17, in_1, xor_6_out);
endmodule
