// Logisim project Odd_parity.circ as structural Verilog: 1 circuit, main circuit main
module main (
  input  in_1,
  input  in_2,
  input  in_3,
  input  in_4,
  input  in_5,
  input  in_6,
  input  in_7,
  input  in_8,
  input  in_9,
  input  in_10,
  input  in_11,
  input  in_12,
  input  in_13,
  input  in_14,
  input  in_15,
  input  in_16,
  input  in_17,
  input  in_18,
  input  in_19,
  input  in_20,
  input  in_21,
  input  in_22,
  output out_23,
  output out_24,
  output out_25
);

  wire odd_parity_1_out, odd_parity_2_out, odd_parity_3_out, odd_parity_4_out, odd_parity_5_out, xor_1_out,
       xor_2_out, xor_3_out, xor_4_out, xor_5_out, xor_6_out, xor_7_out, xor_8_out, xor_9_out, xor_11_out,
       xor_12_out;

  xor xor_1 (xor_1_out, in_2, in_3);
  xor odd_parity_1 (odd_parity_1_out, in_9, in_11);
  xor odd_parity_2 (odd_parity_2_out, in_13, in_15);
  xor odd_parity_3 (odd_parity_3_out, in_17, in_19);
  xor xor_2 (xor_2_out, xor_1_out, in_4);
  xor odd_parity_4 (odd_parity_4_out, odd_parity_1_out, odd_parity_2_out);
  xor odd_parity_5 (odd_parity_5_out, odd_parity_3_out, in_21);
  xor xor_3 (xor_3_out, xor_2_out, in_5);
  xor odd_parity_6 (out_24, odd_parity_4_out, odd_parity_5_out);
  xor xor_4 (xor_4_out, xor_3_out, in_6);
  xor xor_5 (xor_5_out, xor_4_out, in_7);
  xor xor_6 (xor_6_out, in_10, in_12);
  xor xor_7 (xor_7_out, in_14, in_16);
  xor xor_8 (xor_8_out, in_18, in_20);
  xor xor_9 (xor_9_out, xor_5_out, in_8);
  xor xor_10 (out_23, in_1, xor_9_out);
  xor xor_11 (xor_11_out, xor_6_out, xor_7_out);
  xor xor_12 (xor_12_out, xor_8_out, in_22);
  xor xor_13 (out_25, xor_11_out, xor_12_out);
endmodule
