// Logisim project even_parity.circ as structural Verilog: 1 circuit, main circuit main
module main (
  input  in_1,
  input  in_2,
  input  in_3,
  input  in_4,
  input  in_5,
  input  in_6,
  input  in_7,
  input  in_8,
  input  in_9,
  output out_10,
  output out_11,
  output out_12,
  output out_13,
  output out_14
);

  wire and_1_out, and_2_out, not_1_out, not_2_out, xor_1_out, xor_3_out, xor_4_out;

  not not_1 (not_1_out, in_9);
  not not_2 (not_2_out, in_8);
  xor xor_1 (xor_1_out, in_5, in_6);
  and and_1 (and_1_out, in_8, not_1_out);
  and and_2 (and_2_out, not_2_out, in_9);
  or or_1 (out_14, and_1_out, and_2_out);
  xor xor_2 (out_12, xor_1_out, in_7);
  xor xor_3 (xor_3_out, out_12, in_5);
  xor xor_4 (xor_4_out, in_6, in_7);
  xor xor_5 (out_13, xor_3_out, xor_4_out);
  xor odd_parity_1 (out_10, in_1, in_2);
  xnor even_parity_1 (out_11, in_3, in_4);

  // Notes on the sheet:
  //   even parity 생성기
  //   1이 홀수개인 경우 1, 1이 짝수개인 경우 0
  //   even parity 검사기(오류인 경우 1, 정상인 경우 0)
endmodule
