// Logisim project lab02.circ as structural Verilog: 1 circuit, main circuit main
module main (
  input  in_1,
  input  in_2,
  input  in_3,
  input  in_4,
  input  in_5,
  input  in_6,
  input  in_7,
  input  in_8,
  input  in_9,
  input  in_10,
  input  in_11,
  input  in_12,
  output out_13,
  output out_14,
  output out_15
);

  wire and_2_out, and_3_out, and_4_out, and_5_out, and_6_out, or_1_out, or_2_out, or_3_out, or_4_out;

  or or_1 (or_1_out, in_6, in_7);
  or or_2 (or_2_out, in_8, in_9);
  or or_3 (or_3_out, in_9, in_10);
  and and_1 (out_15, or_1_out, or_2_out, or_3_out);
  and and_2 (and_2_out, in_1, in_2);
  or or_4 (or_4_out, in_4, in_5);
  and and_3 (and_3_out, in_1, in_2);
  and and_4 (and_4_out, in_3, in_4);
  and and_5 (and_5_out, in_3, in_5);
  and and_6 (and_6_out, in_3, or_4_out);
  or or_5 (out_14, and_3_out, and_4_out, and_5_out);
  or or_6 (out_13, and_2_out, and_6_out);
endmodule
