// Logisim project lab03.circ as structural Verilog: 6 circuits, main circuit main
module main (
  input  in_1,
  input  in_2,
  input  in_3,
  input  C_in,
  input  A0,
  input  B0,
  input  A1,
  input  B1,
  input  A2,
  input  B2,
  input  A3,
  input  B3,
  input  A4,
  input  B4,
  input  A5,
  input  B5,
  input  A6,
  input  B6,
  input  A7,
  input  B7,
  input  in_21,
  input  in_22,
  input  in_23,
  input  in_24,
  input  in_25,
  input  in_26,
  input  in_27,
  input  in_28,
  input  in_29,
  input  in_30,
  input  in_31,
  input  in_32,
  input  in_33,
  input  in_34,
  input  in_35,
  input  in_36,
  output out_37,
  output out_38,
  output S0,
  output S1,
  output S2,
  output S3,
  output S4,
  output S5,
  output S6,
  output S7,
  output C_out
);

  wire and_1_out, and_2_out, and_6_out, and_7_out, fourbit_adder_1_c_out, xor_1_out;

  xor xor_1 (xor_1_out, in_2, in_3);
  and and_1 (and_1_out, in_2, in_3);
  and and_2 (and_2_out, in_21, in_22);
  // AND_Gate and_3 has open pins: in0=in_24, in1=in_26, out=open
  // AND_Gate and_4 has open pins: in0=in_28, in1=in_30, out=open
  // AND_Gate and_5 has open pins: in0=in_32, in1=in_34, out=open
  xor xor_2 (out_37, in_1, xor_1_out);
  and and_6 (and_6_out, in_1, xor_1_out);
  and and_7 (and_7_out, in_23, in_25);
  // AND_Gate and_8 has open pins: in0=in_27, in1=in_29, out=open
  // AND_Gate and_9 has open pins: in0=in_31, in1=in_33, out=open
  // AND_Gate and_10 has open pins: in0=in_35, in1=in_36, out=open
  or or_1 (out_38, and_6_out, and_1_out);
  fourbit_adder fourbit_adder_1 (
    .C_in(C_in), .A0(A0), .B0(B0), .A1(A1), .B1(B1), .A2(A2), .B2(B2), .A3(A3), .B3(B3), .S0(S0), .S1(S1),
    .S2(S2), .S3(S3), .C_out(fourbit_adder_1_c_out));
  fourbit_adder fourbit_adder_2 (
    .C_in(fourbit_adder_1_c_out), .A0(A4), .B0(B4), .A1(A5), .B1(B5), .A2(A6), .B2(B6), .A3(A7), .B3(B7),
    .S0(S4), .S1(S5), .S2(S6), .S3(S7), .C_out(C_out));
  fourbit_adder fourbit_adder_3 (
    .A0(and_2_out), .B0(and_7_out));  // open: C_in, A1, B1, A2, B2, A3, B3, S0, S1, S2, S3, C_out
endmodule

module halfAdder (
  input  in_1,
  input  in_2,
  input  in_3,
  input  in_4,
  input  in_5,
  input  in_6,
  input  in_7,
  input  in_8,
  output out_9,
  output out_10,
  output out_11,
  output out_12,
  output out_13,
  output out_14,
  output out_15,
  output out_16,
  output out_17
);

  wire and_2_out, and_3_out, and_4_out, not_1_out, not_2_out, not_3_out, not_4_out;

  not not_1 (not_1_out, in_5);
  xor xor_1 (out_9, in_1, in_3);
  and and_1 (out_11, in_1, in_3);
  xor xor_2 (out_13, 1'b1, not_1_out);
  and and_2 (and_2_out, 1'b1, not_1_out);
  not not_2 (not_2_out, in_6);
  xor xor_3 (out_14, and_2_out, not_2_out);
  and and_3 (and_3_out, and_2_out, not_2_out);
  not not_3 (not_3_out, in_7);
  xor xor_4 (out_10, in_2, in_4);
  or or_1 (out_12, in_2, in_4);
  xor xor_5 (out_15, and_3_out, not_3_out);
  and and_4 (and_4_out, and_3_out, not_3_out);
  not not_4 (not_4_out, in_8);
  xor xor_6 (out_16, and_4_out, not_4_out);
  and and_5 (out_17, and_4_out, not_4_out);
endmodule

module fullAdder (
  input  C_in,
  input  A,
  input  B,
  output S,
  output C_out
);

  wire and_1_out, and_2_out, and_3_out;

  xor xor_1 (S, C_in, A, B);
  and and_1 (and_1_out, C_in, A);
  and and_2 (and_2_out, C_in, B);
  and and_3 (and_3_out, A, B);
  xor xor_2 (C_out, and_1_out, and_2_out, and_3_out);
endmodule

module fourbit_adder (
  input  C_in,
  input  A0,
  input  B0,
  input  A1,
  input  B1,
  input  A2,
  input  B2,
  input  A3,
  input  B3,
  output S0,
  output S1,
  output S2,
  output S3,
  output C_out
);

  wire fulladder_1_c_out, fulladder_2_c_out, fulladder_3_c_out;

  fullAdder fulladder_1 (.C_in(C_in), .A(A0), .B(B0), .S(S0), .C_out(fulladder_1_c_out));
  fullAdder fulladder_2 (.C_in(fulladder_1_c_out), .A(A1), .B(B1), .S(S1), .C_out(fulladder_2_c_out));
  fullAdder fulladder_3 (.C_in(fulladder_2_c_out), .A(A2), .B(B2), .S(S2), .C_out(fulladder_3_c_out));
  fullAdder fulladder_4 (.C_in(fulladder_3_c_out), .A(A3), .B(B3), .S(S3), .C_out(C_out));
endmodule

module fourbit_subtractor (
  input  A0,
  input  B0,
  input  A1,
  input  B1,
  input  A2,
  input  B2,
  input  A3,
  input  B3,
  output S0,
  output S1,
  output S2,
  output S3,
  output C_out
);

  wire fulladder_1_c_out, fulladder_2_c_out, fulladder_3_c_out, not_1_out, not_2_out, not_3_out, not_4_out;

  not not_1 (not_1_out, B0);
  not not_2 (not_2_out, B1);
  not not_3 (not_3_out, B2);
  not not_4 (not_4_out, B3);
  fullAdder fulladder_1 (.C_in(1'b1), .A(A0), .B(not_1_out), .S(S0), .C_out(fulladder_1_c_out));
  fullAdder fulladder_2 (.C_in(fulladder_1_c_out), .A(A1), .B(not_2_out), .S(S1), .C_out(fulladder_2_c_out));
  fullAdder fulladder_3 (.C_in(fulladder_2_c_out), .A(A2), .B(not_3_out), .S(S2), .C_out(fulladder_3_c_out));
  fullAdder fulladder_4 (.C_in(fulladder_3_c_out), .A(A3), .B(not_4_out), .S(S3), .C_out(C_out));
endmodule

module fourbit_AdderSubteractor (
  input  S,
  input  A0,
  input  B0,
  input  A1,
  input  B1,
  input  A2,
  input  B2,
  input  A3,
  input  B3,
  output S0,
  output S1,
  output S2,
  output S3,
  output C_out
);

  wire fulladder_1_c_out, fulladder_2_c_out, fulladder_3_c_out, xor_1_out, xor_2_out, xor_3_out, xor_4_out;

  xor xor_1 (xor_1_out, B0, S);
  xor xor_2 (xor_2_out, B1, S);
  xor xor_3 (xor_3_out, B2, S);
  xor xor_4 (xor_4_out, B3, S);
  fullAdder fulladder_1 (.C_in(S), .A(A0), .B(xor_1_out), .S(S0), .C_out(fulladder_1_c_out));
  fullAdder fulladder_2 (.C_in(fulladder_1_c_out), .A(A1), .B(xor_2_out), .S(S1), .C_out(fulladder_2_c_out));
  fullAdder fulladder_3 (.C_in(fulladder_2_c_out), .A(A2), .B(xor_3_out), .S(S2), .C_out(fulladder_3_c_out));
  fullAdder fulladder_4 (.C_in(fulladder_3_c_out), .A(A3), .B(xor_4_out), .S(S3), .C_out(C_out));
endmodule
