// Logisim project lab04.circ as structural Verilog: 2 circuits, main circuit main
module main (
  input  in_1,
  input  in_2,
  input  in_3,
  input  in_4,
  input  in_5,
  input  in_6,
  input  in_7,
  input  in_8,
  input  in_9,
  input  in_10,
  input  in_11,
  input  in_12,
  input  in_13,
  input  in_14,
  input  in_15,
  input  in_16,
  output out_17,
  output out_18,
  output out_19,
  output out_20
);

  wire and_1_out, and_2_out, and_3_out, nand_1_out, nand_2_out, nand_3_out, nand_4_out, nand_5_out,
       nand_6_out, nand_7_out, nand_8_out, nand_9_out, nand_10_out, nand_11_out, nand_12_out, nand_13_out,
       nand_14_out, nand_15_out, not_1_out, not_2_out, not_3_out;

  not not_1 (not_1_out, in_1);
  not not_2 (not_2_out, in_4);
  nand nand_1 (nand_1_out, in_5, in_7, in_8);
  and and_1 (and_1_out, in_9, in_11);
  not not_3 (not_3_out, in_12);
  nand nand_2 (nand_2_out, in_13, in_15);
  and and_2 (and_2_out, in_1, in_3, in_4);
  nand nand_3 (nand_3_out, in_5, in_5);
  nand nand_4 (nand_4_out, in_8, in_8);
  nand nand_5 (nand_5_out, in_16, in_16);
  and and_3 (and_3_out, in_2, not_1_out);
  nand nand_6 (nand_6_out, nand_1_out, nand_1_out);
  nand nand_7 (nand_7_out, in_6, nand_3_out);
  ExactlyOne xor_1 (.out(out_19), .in0(and_1_out), .in1(in_10), .in2(not_3_out));
  nand nand_8 (nand_8_out, nand_2_out, nand_2_out);
  or or_1 (out_17, and_2_out, and_3_out, not_2_out);
  nand nand_9 (nand_9_out, nand_6_out, nand_6_out);
  nand nand_10 (nand_10_out, nand_7_out, nand_7_out);
  nand nand_11 (nand_11_out, nand_4_out, nand_4_out);
  nand nand_12 (nand_12_out, nand_8_out, nand_8_out);
  nand nand_13 (nand_13_out, in_14, in_14);
  nand nand_14 (nand_14_out, nand_5_out, nand_5_out);
  nand nand_15 (nand_15_out, nand_10_out, nand_10_out);
  nand nand_16 (out_18, nand_9_out, nand_15_out, nand_11_out);
  nand nand_17 (out_20, nand_12_out, nand_13_out, nand_14_out);
endmodule

module first (
  input  a,
  input  b,
  input  c,
  input  d,
  output o
);

  wire nand_1_out, nand_2_out, nand_3_out;

  nand nand_1 (nand_1_out, 1'b1, a);
  nand nand_2 (nand_2_out, nand_1_out, b);
  nand nand_3 (nand_3_out, a, c);
  nand nand_4 (o, d, nand_2_out, nand_3_out);
endmodule
